// Logisim project CompBasedArchUlt.circ as structural Verilog: 2 circuits, main circuit main
module main (
  input  in_1,
  input  in_2,
  input  in_3,
  input  in_4,
  input  in_5,
  input  in_6,
  input  in_7,
  input  in_8,
  input  in_9,
  input  in_10,
  input  in_11,
  input  in_12,
  input  in_13,
  input  in_14,
  input  in_15,
  input  in_16,
  input  in_17,
  input  in_18,
  input  in_19,
  input  in_20,
  input  in_21,
  input  in_22,
  input  in_23,
  input  in_24,
  input  in_25,
  input  in_26,
  input  in_27
);

  wire clock_1_out;
  wire [3:0] registers_1_out_11, undriven_2, undriven_3;
  wire [7:0] registers_1_out_7, registers_1_out_8, registers_1_out_9, registers_1_out_10, registers_1_out_12,
       registers_1_out_13, registers_1_out_14, registers_1_out_15, undriven, undriven_4, undriven_5;
  wire [7:4] registers_1_out_11_2;

  registers registers_1 (
    .in_2(clock_1_out), .in_3(in_11), .in_5(in_15), .in_1(registers_1_out_7),
    .in_4({in_1, in_2, in_3, in_4, in_5, in_12, in_13, in_14}),
    .in_6({in_6, in_7, in_8, in_9, in_10, in_16, in_17, in_18}), .out_10(registers_1_out_10),
    .out_11({registers_1_out_11_2, registers_1_out_11}), .out_12(registers_1_out_12),
    .out_13(registers_1_out_13), .out_14(registers_1_out_14), .out_15(registers_1_out_15),
    .out_7(registers_1_out_7), .out_8(registers_1_out_8), .out_9(registers_1_out_9));
  Clock clock_1 (.out(clock_1_out));
  assign registers_1_out_7 = in_27 ? {in_19, in_20, in_21, in_22, in_23, in_24, in_25, in_26} : 8'bz;  // Controlled_Buffer controlled_buffer_1
  Hex_Digit_Display hex_digit_display_1 (.value(registers_1_out_7[7:4]));  // open: dp
  Hex_Digit_Display hex_digit_display_2 (.value(registers_1_out_8[7:4]));  // open: dp
  Hex_Digit_Display hex_digit_display_3 (.value(registers_1_out_7[3:0]));  // open: dp
  Hex_Digit_Display hex_digit_display_4 (.value(registers_1_out_8[3:0]));  // open: dp
  Hex_Digit_Display hex_digit_display_5 (.value(registers_1_out_9[7:4]));  // open: dp
  Hex_Digit_Display hex_digit_display_6 (.value(undriven[7:4]));  // open: dp
  Hex_Digit_Display hex_digit_display_7 (.value(registers_1_out_9[3:0]));  // open: dp
  Hex_Digit_Display hex_digit_display_8 (.value(registers_1_out_10[7:4]));  // open: dp
  Hex_Digit_Display hex_digit_display_9 (.value(undriven[3:0]));  // open: dp
  Hex_Digit_Display hex_digit_display_10 (.value(undriven_4[7:4]));  // open: dp
  Hex_Digit_Display hex_digit_display_11 (.value(registers_1_out_10[3:0]));  // open: dp
  Hex_Digit_Display hex_digit_display_12 (.value(undriven_4[3:0]));  // open: dp
  Hex_Digit_Display hex_digit_display_13 (.value(undriven_5[7:4]));  // open: dp
  Hex_Digit_Display hex_digit_display_14 (.value(registers_1_out_11));  // open: dp
  Hex_Digit_Display hex_digit_display_15 (.value(registers_1_out_11_2));  // open: dp
  Hex_Digit_Display hex_digit_display_16 (.value(undriven_5[3:0]));  // open: dp
  Hex_Digit_Display hex_digit_display_17 (.value(undriven_3));  // open: dp
  Hex_Digit_Display hex_digit_display_18 (.value(undriven_2));  // open: dp
endmodule

module registers (
  input  [7:0] in_1,
  input  in_2,
  input  in_3,
  input  [7:0] in_4,
  input  in_5,
  input  [7:0] in_6,
  output [7:0] out_7,
  output [7:0] out_8,
  output [7:0] out_9,
  output [7:0] out_10,
  output [7:0] out_11,
  output [7:0] out_12,
  output [7:0] out_13,
  output [7:0] out_14,
  output [7:0] out_15
);

  wire decoder_1_out0, decoder_1_out1, decoder_1_out2, decoder_1_out3, decoder_1_out4, decoder_1_out5,
       decoder_1_out6, decoder_1_out7, decoder_2_out0, decoder_2_out1, decoder_2_out2, decoder_2_out3,
       decoder_2_out4, decoder_2_out5, decoder_2_out6, decoder_2_out7;
  wire [2:0] bitselector_1_out, bitselector_2_out;

  Decoder #(.select(3)) decoder_1 (
    .out0(decoder_1_out0), .out1(decoder_1_out1), .out2(decoder_1_out2), .out3(decoder_1_out3),
    .out4(decoder_1_out4), .out5(decoder_1_out5), .out6(decoder_1_out6), .out7(decoder_1_out7),
    .sel(bitselector_1_out), .en(in_3));
  BitSelector #(.group(3)) bitselector_1 (.in(in_4), .out(bitselector_1_out), .sel(2'b00));
  Decoder #(.select(3)) decoder_2 (
    .out0(decoder_2_out0), .out1(decoder_2_out1), .out2(decoder_2_out2), .out3(decoder_2_out3),
    .out4(decoder_2_out4), .out5(decoder_2_out5), .out6(decoder_2_out6), .out7(decoder_2_out7),
    .sel(bitselector_2_out), .en(in_5));
  BitSelector #(.group(3)) bitselector_2 (.in(in_6), .out(bitselector_2_out), .sel(2'b00));
  assign out_7 = decoder_2_out0 ? out_8 : 8'bz;  // Controlled_Buffer controlled_buffer_1
  Register register_1 (.D(in_1), .en(decoder_1_out0), .Q(out_8), .clk(in_2));  // open: clr
  Register register_2 (.D(in_1), .en(decoder_1_out1), .Q(out_9), .clk(in_2));  // open: clr
  assign out_7 = decoder_2_out1 ? out_9 : 8'bz;  // Controlled_Buffer controlled_buffer_2
  Register register_3 (.D(in_1), .en(decoder_1_out2), .Q(out_10), .clk(in_2));  // open: clr
  assign out_7 = decoder_2_out2 ? out_10 : 8'bz;  // Controlled_Buffer controlled_buffer_3
  Register register_4 (.D(in_1), .en(decoder_1_out3), .Q(out_11), .clk(in_2));  // open: clr
  assign out_7 = decoder_2_out3 ? out_11 : 8'bz;  // Controlled_Buffer controlled_buffer_4
  Register register_5 (.D(in_1), .en(decoder_1_out4), .Q(out_12), .clk(in_2));  // open: clr
  assign out_7 = decoder_2_out4 ? out_12 : 8'bz;  // Controlled_Buffer controlled_buffer_5
  Register register_6 (.D(in_1), .en(decoder_1_out5), .Q(out_13), .clk(in_2));  // open: clr
  assign out_7 = decoder_2_out5 ? out_13 : 8'bz;  // Controlled_Buffer controlled_buffer_6
  Register register_7 (.D(in_1), .en(decoder_1_out6), .Q(out_14), .clk(in_2));  // open: clr
  assign out_7 = decoder_2_out6 ? out_14 : 8'bz;  // Controlled_Buffer controlled_buffer_7
  assign out_7 = decoder_2_out7 ? out_15 : 8'bz;  // Controlled_Buffer controlled_buffer_8
  Register register_8 (.D(in_1), .en(decoder_1_out7), .Q(out_15), .clk(in_2));  // open: clr
endmodule
